// Logisim project cpu.circ as structural Verilog: 10 circuits, main circuit main
module main (
  input  reset
);

  wire alu_3_zero, and_1_out, and_2_out, beq, bgez, branch, clk, decoder_1_out0, decoder_1_out1,
       decoder_1_out2, decoder_1_out3, decoder_1_out4, decoder_1_out5, decoder_1_out6, decoder_1_out7,
       decoder_1_out13, decoder_1_out14, iType, j, jal, jr, keyboard_1_avail, lw, memory_latch_1_oe_latched,
       memory_latch_1_we_latched, not_1_out, not_2_out, not_4_out, not_5_out, or_3_out, readKey, regWE, sw,
       TTYinput;
  wire [2:0] aluOpcode, multiplexer_1_out, multiplexer_3_out;
  wire [3:3] Opcode;
  wire [6:0] bit_extender_1_out;
  wire [7:0] ascii_key;
  wire [11:0] Adress, instruction_memory_data;
  wire [15:0] alu_2_outputdata, alu_4_outputdata, bit_extender_3_out, jalVal, memory_latch_1_address_latched,
       memory_latch_1_data_in_latched, multiplexer_2_out, multiplexer_4_out, multiplexer_5_out,
       multiplexer_6_out, multiplexer_7_out, multiplexer_8_out, multiplexer_9_out, PC_dataout, ram_1_dout,
       rs1val, rs2val, signExtendedImm;

  Clock clock_1 (.out(clk));
  not not_1 (not_1_out, clk);
  simpleRegister PC (
    .dataIn(multiplexer_2_out), .clk(not_1_out), .writeEnable(1'b1), .reset(reset), .dataOut(PC_dataout));
  // Probe on PC_dataout
  ROM #(.addrWidth(16), .dataWidth(16)) instruction_memory (
    .addr(PC_dataout), .data({Opcode[3], aluOpcode, instruction_memory_data}));
  Bit_Extender #(.in_width(16), .out_width(7), .\type ("zero")) bit_extender_1 (.in(rs1val), .out(bit_extender_1_out));
  not not_2 (not_2_out, clk);
  TTY #(.rows(13), .cols(80)) tty_1 (.data(bit_extender_1_out), .clk(clk), .we(TTYinput), .clr(reset));
  ALU alu_1 (.InputData2(16'h1), .OpType(3'b000), .InputData1(PC_dataout), .OutputData(jalVal));  // open: Shamt, zero
  Keyboard keyboard_1 (.clk(not_2_out), .re(readKey), .clr(reset), .avail(keyboard_1_avail), .data(ascii_key[6:0]));
  not not_3 (ascii_key[7], keyboard_1_avail);
  // Probe on multiplexer_2_out
  // Probe on jalVal
  Multiplexer #(.width(3), .enable("false")) multiplexer_1 (
    .in0(Adress[5:3]), .in1(Adress[8:6]), .out(multiplexer_1_out), .sel(iType));
  Multiplexer #(.width(16), .enable("false")) multiplexer_2 (
    .in0(multiplexer_8_out), .in1(rs1val), .out(multiplexer_2_out), .sel(jr));
  // Probe on multiplexer_4_out
  Multiplexer #(.width(3), .enable("false")) multiplexer_3 (
    .in0(multiplexer_1_out), .in1(3'b111), .out(multiplexer_3_out), .sel(jal));
  // Probe on multiplexer_3_out
  InstructionDecode instructiondecode_1 (
    .input_16_bits({Opcode[3], aluOpcode, instruction_memory_data}), .Shamt(Adress[2:0]), .Rd(Adress[5:3]),
    .Rt(Adress[8:6]), .Rs(Adress[11:9]), .lw(lw), .sw(sw), .iType(iType), .bgez(bgez), .beq(beq),
    .readKeyboard(readKey), .TTY(TTYinput), .j(j), .jr(jr), .jal(jal));
  // Probe on Adress[8:6]
  // Probe on Adress[11:9]
  // Probe on Adress[5:3]
  Multiplexer #(.width(16), .enable("false")) multiplexer_4 (
    .in0(multiplexer_5_out), .in1(jalVal), .out(multiplexer_4_out), .sel(jal));
  Multiplexer #(.width(16), .enable("false")) multiplexer_5 (
    .in0(multiplexer_9_out), .in1({{8{1'b0}}, ascii_key}), .out(multiplexer_5_out), .sel(readKey));
  Decoder #(.select(4)) decoder_1 (
    .out0(decoder_1_out0), .out1(decoder_1_out1), .out2(decoder_1_out2), .out3(decoder_1_out3),
    .out4(decoder_1_out4), .out5(decoder_1_out5), .out6(decoder_1_out6), .out7(decoder_1_out7),
    .out13(decoder_1_out13), .out14(decoder_1_out14), .sel({Opcode[3], aluOpcode}));  // open: out8, out9, out10, out11, out12, out15, en
  // Probe on rs1val
  RegisterFile registerfile_1 (
    .rs1val(rs1val), .ReadReg2(Adress[8:6]), .clk(clk), .ReadReg1(Adress[11:9]), .reset(reset),
    .WritePort(multiplexer_3_out), .WriteData(multiplexer_4_out), .WE(regWE), .rs2val(rs2val));
  // Probe on rs2val
  assign signExtendedImm = {{10{Adress[5]}}, Adress[5:0]};  // Bit_Extender bit_extender_2
  Multiplexer #(.width(16), .enable("false")) multiplexer_6 (
    .in0(rs2val), .in1(signExtendedImm), .out(multiplexer_6_out), .sel(iType));
  // Probe on multiplexer_6_out
  // Probe on aluOpcode
  ALU alu_2 (
    .InputData2(signExtendedImm), .OpType(3'b000), .InputData1(jalVal), .OutputData(alu_2_outputdata));  // open: Shamt, zero
  // Probe on signExtendedImm
  or or_1 (regWE, decoder_1_out0, decoder_1_out1, decoder_1_out2, decoder_1_out3, decoder_1_out4, decoder_1_out5, decoder_1_out6, decoder_1_out7, decoder_1_out13, decoder_1_out14);
  ALU alu_3 (.InputData2(rs2val), .InputData1(rs1val), .zero(alu_3_zero));  // open: OpType, Shamt, OutputData
  Multiplexer #(.width(16), .enable("false")) multiplexer_7 (
    .in0(jalVal), .in1(alu_2_outputdata), .out(multiplexer_7_out), .sel(branch));
  ALU alu_4 (
    .InputData2(multiplexer_6_out), .OpType(aluOpcode), .InputData1(rs1val), .Shamt(Adress[2:0]),
    .OutputData(alu_4_outputdata));  // open: zero
  and and_1 (and_1_out, beq, alu_3_zero);
  and and_2 (and_2_out, bgez, not_4_out);
  assign bit_extender_3_out = {{4{Adress[11]}}, Adress};  // Bit_Extender bit_extender_3
  // Probe on alu_4_outputdata
  or or_2 (branch, and_1_out, and_2_out);
  not not_4 (not_4_out, rs1val[15]);
  Multiplexer #(.width(16), .enable("false")) multiplexer_8 (
    .in0(multiplexer_7_out), .in1(bit_extender_3_out), .out(multiplexer_8_out), .sel(or_3_out));
  or or_3 (or_3_out, jal, j);
  not not_5 (not_5_out, clk);
  memory_latch memory_latch_1 (
    .address(alu_4_outputdata), .WE(sw), .clk(not_5_out), .data_in(rs2val),
    .address_latched(memory_latch_1_address_latched), .WE_latched(memory_latch_1_we_latched),
    .OE_latched(memory_latch_1_oe_latched), .data_in_latched(memory_latch_1_data_in_latched));
  RAM #(.addrWidth(16), .dataWidth(16), .trigger("high"), .databus("bibus")) ram_1 (
    .addr(memory_latch_1_address_latched), .we(memory_latch_1_we_latched), .oe(memory_latch_1_oe_latched),
    .din(memory_latch_1_data_in_latched), .dout(ram_1_dout));
  Multiplexer #(.width(16), .enable("false")) multiplexer_9 (
    .in0(alu_4_outputdata), .in1(ram_1_dout), .out(multiplexer_9_out), .sel(lw));

  // Other names for the same wires on the sheet: Opcode[2:0] = aluOpcode; Imm[5:0] = Adress[5:0];
  //   Shamt[2:0] = Adress[2:0]; Rd[2:0] = Adress[5:3]; Rt[2:0] = Adress[8:6]; Rs[2:0] = Adress[11:9];
  //   normPC[15:0] = jalVal

  // Notes on the sheet:
  //   contents of instruction_memory (hex, n*v repeats v):
  //   83 c4 101 8880 88c1
  //   Data out ->
endmodule

module simpleRegister (
  input  [15:0] dataIn,
  input  clk,
  input  writeEnable,
  input  reset,
  output [15:0] dataOut
);

  wire clk_t;

  and and_1 (clk_t, clk, writeEnable);
  D_Flip_Flop d_ff_1 (.D(dataIn[0]), .clk(clk_t), .Q(dataOut[0]), .reset(reset));  // open: Qn, preset
  D_Flip_Flop d_ff_2 (.D(dataIn[1]), .clk(clk_t), .Q(dataOut[1]), .reset(reset));  // open: Qn, preset
  D_Flip_Flop d_ff_3 (.D(dataIn[2]), .clk(clk_t), .Q(dataOut[2]), .reset(reset));  // open: Qn, preset
  D_Flip_Flop d_ff_4 (.D(dataIn[3]), .clk(clk_t), .Q(dataOut[3]), .reset(reset));  // open: Qn, preset
  D_Flip_Flop d_ff_5 (.D(dataIn[4]), .clk(clk_t), .Q(dataOut[4]), .reset(reset));  // open: Qn, preset
  D_Flip_Flop d_ff_6 (.D(dataIn[5]), .clk(clk_t), .Q(dataOut[5]), .reset(reset));  // open: Qn, preset
  D_Flip_Flop d_ff_7 (.D(dataIn[6]), .clk(clk_t), .Q(dataOut[6]), .reset(reset));  // open: Qn, preset
  D_Flip_Flop d_ff_8 (.D(dataIn[7]), .clk(clk_t), .Q(dataOut[7]), .reset(reset));  // open: Qn, preset
  D_Flip_Flop d_ff_9 (.D(dataIn[8]), .clk(clk_t), .Q(dataOut[8]), .reset(reset));  // open: Qn, preset
  D_Flip_Flop d_ff_10 (.D(dataIn[9]), .clk(clk_t), .Q(dataOut[9]), .reset(reset));  // open: Qn, preset
  D_Flip_Flop d_ff_11 (.D(dataIn[10]), .clk(clk_t), .Q(dataOut[10]), .reset(reset));  // open: Qn, preset
  D_Flip_Flop d_ff_12 (.D(dataIn[11]), .clk(clk_t), .Q(dataOut[11]), .reset(reset));  // open: Qn, preset
  D_Flip_Flop d_ff_13 (.D(dataIn[12]), .clk(clk_t), .Q(dataOut[12]), .reset(reset));  // open: Qn, preset
  D_Flip_Flop d_ff_14 (.D(dataIn[13]), .clk(clk_t), .Q(dataOut[13]), .reset(reset));  // open: Qn, preset
  D_Flip_Flop d_ff_15 (.D(dataIn[14]), .clk(clk_t), .Q(dataOut[14]), .reset(reset));  // open: Qn, preset
  D_Flip_Flop d_ff_16 (.D(dataIn[15]), .clk(clk_t), .Q(dataOut[15]), .reset(reset));  // open: Qn, preset

  // Other names for the same wires on the sheet: in0 = dataIn[0]; in1 = dataIn[1]; in2 = dataIn[2]; in3 = dataIn[3];
  //   in4 = dataIn[4]; in5 = dataIn[5]; in6 = dataIn[6]; in7 = dataIn[7]; in8 = dataIn[8]; in9 = dataIn[9];
  //   in10 = dataIn[10]; in11 = dataIn[11]; in12 = dataIn[12]; in13 = dataIn[13]; in14 = dataIn[14];
  //   in15 = dataIn[15]; out0 = dataOut[0]; out1 = dataOut[1]; out2 = dataOut[2]; out3 = dataOut[3];
  //   out4 = dataOut[4]; out5 = dataOut[5]; out6 = dataOut[6]; out7 = dataOut[7]; out8 = dataOut[8];
  //   out9 = dataOut[9]; out10 = dataOut[10]; out11 = dataOut[11]; out12 = dataOut[12]; out13 = dataOut[13];
  //   out14 = dataOut[14]; out15 = dataOut[15]
endmodule

module ALU (
  input  [15:0] InputData2,
  input  [2:0] OpType,
  input  [15:0] InputData1,
  input  [2:0] Shamt,
  output [15:0] OutputData,
  output zero
);

  wire or_1_out;
  wire [15:0] and_1_out, full_adder_1_result, full_adder_2_result, full_adder_3_result,
       left_shift_1_shifted_out, not_1_out, right_shift_1_shifted_out;

  left_shift left_shift_1 (.bitsIn(InputData1), .Shamt(Shamt), .shifted_out(left_shift_1_shifted_out));
  right_shift right_shift_1 (.Shamt(Shamt), .bitsIn(InputData1), .shifted_out(right_shift_1_shifted_out));
  assign not_1_out = ~InputData1;  // NOT_Gate not_1, 16 bits wide
  assign and_1_out = InputData2 & InputData1;  // AND_Gate and_1, 16 bits wide
  full_adder full_adder_1 (.B(InputData2), .A(InputData1), .result(full_adder_1_result));  // open: ovf, sub
  full_adder full_adder_2 (.sub(1'b1), .B(InputData2), .A(InputData1), .result(full_adder_2_result));  // open: ovf
  Multiplexer #(.select(3), .width(16), .enable("false")) multiplexer_1 (
    .in0(full_adder_1_result), .in1(full_adder_2_result), .in2(full_adder_1_result), .in3(not_1_out),
    .in4(and_1_out), .in5(left_shift_1_shifted_out), .in6(right_shift_1_shifted_out),
    .in7(full_adder_1_result), .out(OutputData), .sel(OpType));
  full_adder full_adder_3 (.sub(1'b1), .B(InputData2), .A(InputData1), .result(full_adder_3_result));  // open: ovf
  or or_1 (or_1_out, full_adder_3_result[0], full_adder_3_result[1], full_adder_3_result[2], full_adder_3_result[3], full_adder_3_result[4], full_adder_3_result[5], full_adder_3_result[6], full_adder_3_result[7], full_adder_3_result[8], full_adder_3_result[9], full_adder_3_result[10], full_adder_3_result[11], full_adder_3_result[12], full_adder_3_result[13], full_adder_3_result[14], full_adder_3_result[15]);
  not not_2 (zero, or_1_out);

  // Other names for the same wires on the sheet: in1[15:0] = InputData1; in2[15:0] = InputData2

  // Notes on the sheet:
  //   001 -> sub
  //   011 -> not
  //   000 -> addi
  //   100 -> and
  //   101 -> sll
  //   110 -> srl
  //   111 -> sw (same as addi)
  //   010 -> add
endmodule

module RegisterFile (
  input  clk,
  input  reset,
  input  [15:0] WriteData,
  input  WE,
  input  [2:0] WritePort,
  input  [2:0] ReadReg1,
  input  [2:0] ReadReg2,
  output [15:0] rs1val,
  output [15:0] rs2val
);

  wire RS0, RS1, RS2, RS3, RS4, RS5, RS6, RS7, RT0, RT1, RT2, RT3, RT4, RT5, RT6, RT7, WE0, WE1, WE2, WE3,
       WE4, WE5, WE6, WE7;
  wire [15:0] simpleregister_1_dataout, simpleregister_2_dataout, simpleregister_3_dataout,
       simpleregister_4_dataout, simpleregister_5_dataout, simpleregister_6_dataout, simpleregister_7_dataout;

  Decoder #(.select(3)) decoder_1 (
    .out0(WE0), .out1(WE1), .out2(WE2), .out3(WE3), .out4(WE4), .out5(WE5), .out6(WE6), .out7(WE7),
    .sel(WritePort), .en(WE));
  Decoder #(.select(3)) decoder_2 (
    .out0(RS0), .out1(RS1), .out2(RS2), .out3(RS3), .out4(RS4), .out5(RS5), .out6(RS6), .out7(RS7),
    .sel(ReadReg1));  // open: en
  Decoder #(.select(3)) decoder_3 (
    .out0(RT0), .out1(RT1), .out2(RT2), .out3(RT3), .out4(RT4), .out5(RT5), .out6(RT6), .out7(RT7),
    .sel(ReadReg2));  // open: en
  // Probe on {16{1'b0}}
  // Probe on simpleregister_1_dataout
  simpleRegister simpleregister_1 (
    .dataIn(WriteData), .clk(clk), .writeEnable(WE1), .reset(reset), .dataOut(simpleregister_1_dataout));
  // Probe on simpleregister_2_dataout
  simpleRegister simpleregister_2 (
    .dataIn(WriteData), .clk(clk), .writeEnable(WE2), .reset(reset), .dataOut(simpleregister_2_dataout));
  // Probe on simpleregister_3_dataout
  simpleRegister simpleregister_3 (
    .dataIn(WriteData), .clk(clk), .writeEnable(WE3), .reset(reset), .dataOut(simpleregister_3_dataout));
  // Probe on simpleregister_4_dataout
  simpleRegister simpleregister_4 (
    .dataIn(WriteData), .clk(clk), .writeEnable(WE4), .reset(reset), .dataOut(simpleregister_4_dataout));
  // Probe on simpleregister_5_dataout
  simpleRegister simpleregister_5 (
    .dataIn(WriteData), .clk(clk), .writeEnable(WE5), .reset(reset), .dataOut(simpleregister_5_dataout));
  // Probe on simpleregister_6_dataout
  simpleRegister simpleregister_6 (
    .dataIn(WriteData), .clk(clk), .writeEnable(WE6), .reset(reset), .dataOut(simpleregister_6_dataout));
  // Probe on simpleregister_7_dataout
  simpleRegister simpleregister_7 (
    .dataIn(WriteData), .clk(clk), .writeEnable(WE7), .reset(reset), .dataOut(simpleregister_7_dataout));
  assign rs2val = RT0 ? {16{1'b0}} : 16'bz;  // Controlled_Buffer controlled_buffer_1
  assign rs2val = RT1 ? simpleregister_1_dataout : 16'bz;  // Controlled_Buffer controlled_buffer_2
  assign rs2val = RT2 ? simpleregister_2_dataout : 16'bz;  // Controlled_Buffer controlled_buffer_3
  assign rs2val = RT3 ? simpleregister_3_dataout : 16'bz;  // Controlled_Buffer controlled_buffer_4
  assign rs2val = RT4 ? simpleregister_4_dataout : 16'bz;  // Controlled_Buffer controlled_buffer_5
  assign rs2val = RT5 ? simpleregister_5_dataout : 16'bz;  // Controlled_Buffer controlled_buffer_6
  assign rs2val = RT6 ? simpleregister_6_dataout : 16'bz;  // Controlled_Buffer controlled_buffer_7
  assign rs2val = RT7 ? simpleregister_7_dataout : 16'bz;  // Controlled_Buffer controlled_buffer_8
  assign rs1val = RS0 ? {16{1'b0}} : 16'bz;  // Controlled_Buffer controlled_buffer_9
  assign rs1val = RS1 ? simpleregister_1_dataout : 16'bz;  // Controlled_Buffer controlled_buffer_10
  assign rs1val = RS2 ? simpleregister_2_dataout : 16'bz;  // Controlled_Buffer controlled_buffer_11
  assign rs1val = RS3 ? simpleregister_3_dataout : 16'bz;  // Controlled_Buffer controlled_buffer_12
  assign rs1val = RS4 ? simpleregister_4_dataout : 16'bz;  // Controlled_Buffer controlled_buffer_13
  assign rs1val = RS5 ? simpleregister_5_dataout : 16'bz;  // Controlled_Buffer controlled_buffer_14
  assign rs1val = RS6 ? simpleregister_6_dataout : 16'bz;  // Controlled_Buffer controlled_buffer_15
  assign rs1val = RS7 ? simpleregister_7_dataout : 16'bz;  // Controlled_Buffer controlled_buffer_16
endmodule

module full_adder (
  input  [15:0] B,
  input  [15:0] A,
  input  sub,
  output [15:0] result,
  output ovf
);

  wire simpleadder_1_cout, simpleadder_2_cout, simpleadder_3_cout, simpleadder_4_cout, simpleadder_5_cout,
       simpleadder_6_cout, simpleadder_7_cout, simpleadder_8_cout, simpleadder_9_cout, simpleadder_10_cout,
       simpleadder_11_cout, simpleadder_12_cout, simpleadder_13_cout, simpleadder_14_cout,
       simpleadder_15_cout, simpleadder_16_cout, xor_1_out, xor_2_out, xor_3_out, xor_4_out, xor_5_out,
       xor_6_out, xor_7_out, xor_8_out, xor_9_out, xor_10_out, xor_11_out, xor_12_out, xor_13_out,
       xor_14_out, xor_15_out, xor_16_out;

  xor xor_1 (xor_1_out, B[0], sub);
  xor xor_2 (xor_2_out, B[4], sub);
  xor xor_3 (xor_3_out, B[8], sub);
  xor xor_4 (xor_4_out, B[12], sub);
  simpleAdder simpleadder_1 (.a(xor_1_out), .b(A[0]), .Cin(sub), .res(result[0]), .Cout(simpleadder_1_cout));
  simpleAdder simpleadder_2 (
    .a(xor_3_out), .b(A[8]), .Cin(simpleadder_14_cout), .res(result[8]), .Cout(simpleadder_2_cout));
  simpleAdder simpleadder_3 (
    .a(xor_4_out), .b(A[12]), .Cin(simpleadder_15_cout), .res(result[12]), .Cout(simpleadder_3_cout));
  xor xor_5 (xor_5_out, B[1], sub);
  simpleAdder simpleadder_4 (
    .a(xor_2_out), .b(A[4]), .Cin(simpleadder_13_cout), .res(result[4]), .Cout(simpleadder_4_cout));
  xor xor_6 (xor_6_out, B[5], sub);
  xor xor_7 (xor_7_out, B[9], sub);
  xor xor_8 (xor_8_out, B[13], sub);
  simpleAdder simpleadder_5 (
    .a(xor_5_out), .b(A[1]), .Cin(simpleadder_1_cout), .res(result[1]), .Cout(simpleadder_5_cout));
  simpleAdder simpleadder_6 (
    .a(xor_6_out), .b(A[5]), .Cin(simpleadder_4_cout), .res(result[5]), .Cout(simpleadder_6_cout));
  simpleAdder simpleadder_7 (
    .a(xor_7_out), .b(A[9]), .Cin(simpleadder_2_cout), .res(result[9]), .Cout(simpleadder_7_cout));
  simpleAdder simpleadder_8 (
    .a(xor_8_out), .b(A[13]), .Cin(simpleadder_3_cout), .res(result[13]), .Cout(simpleadder_8_cout));
  xor xor_9 (xor_9_out, B[2], sub);
  xor xor_10 (xor_10_out, B[6], sub);
  xor xor_11 (xor_11_out, B[10], sub);
  xor xor_12 (xor_12_out, B[14], sub);
  simpleAdder simpleadder_9 (
    .a(xor_9_out), .b(A[2]), .Cin(simpleadder_5_cout), .res(result[2]), .Cout(simpleadder_9_cout));
  simpleAdder simpleadder_10 (
    .a(xor_10_out), .b(A[6]), .Cin(simpleadder_6_cout), .res(result[6]), .Cout(simpleadder_10_cout));
  simpleAdder simpleadder_11 (
    .a(xor_11_out), .b(A[10]), .Cin(simpleadder_7_cout), .res(result[10]), .Cout(simpleadder_11_cout));
  simpleAdder simpleadder_12 (
    .a(xor_12_out), .b(A[14]), .Cin(simpleadder_8_cout), .res(result[14]), .Cout(simpleadder_12_cout));
  xor xor_13 (xor_13_out, B[3], sub);
  xor xor_14 (xor_14_out, B[7], sub);
  xor xor_15 (xor_15_out, B[11], sub);
  xor xor_16 (xor_16_out, B[15], sub);
  simpleAdder simpleadder_13 (
    .a(xor_13_out), .b(A[3]), .Cin(simpleadder_9_cout), .res(result[3]), .Cout(simpleadder_13_cout));
  simpleAdder simpleadder_14 (
    .a(xor_14_out), .b(A[7]), .Cin(simpleadder_10_cout), .res(result[7]), .Cout(simpleadder_14_cout));
  simpleAdder simpleadder_15 (
    .a(xor_15_out), .b(A[11]), .Cin(simpleadder_11_cout), .res(result[11]), .Cout(simpleadder_15_cout));
  simpleAdder simpleadder_16 (
    .a(xor_16_out), .b(A[15]), .Cin(simpleadder_12_cout), .res(result[15]), .Cout(simpleadder_16_cout));
  xor xor_17 (ovf, simpleadder_16_cout, simpleadder_12_cout);

  // Other names for the same wires on the sheet: b0 = A[0]; b1 = A[1]; b2 = A[2]; b3 = A[3]; b4 = A[4]; b5 = A[5];
  //   b6 = A[6]; b7 = A[7]; b8 = A[8]; b9 = A[9]; b10 = A[10]; b11 = A[11]; b12 = A[12]; b13 = A[13]; b14 = A[14];
  //   b15 = A[15]; a0 = B[0]; a1 = B[1]; a2 = B[2]; a3 = B[3]; a4 = B[4]; a5 = B[5]; a6 = B[6]; a7 = B[7]; a8 = B[8];
  //   a9 = B[9]; a10 = B[10]; a11 = B[11]; a12 = B[12]; a13 = B[13]; a14 = B[14]; a15 = B[15]
endmodule

module simpleAdder (
  input  a,
  input  b,
  input  Cin,
  output res,
  output Cout
);

  wire and_1_out, and_2_out, xor_1_out;

  and and_1 (and_1_out, b, a);
  xor xor_1 (xor_1_out, a, b);
  and and_2 (and_2_out, xor_1_out, Cin);
  xor xor_2 (res, Cin, xor_1_out);
  or or_1 (Cout, and_2_out, and_1_out);
endmodule

module right_shift (
  input  [15:0] bitsIn,
  input  [2:0] Shamt,
  output [15:0] shifted_out
);

  wire multiplexer_1_out, multiplexer_2_out, multiplexer_3_out, multiplexer_4_out, multiplexer_5_out,
       multiplexer_6_out, multiplexer_7_out, multiplexer_8_out, multiplexer_9_out, multiplexer_10_out,
       multiplexer_11_out, multiplexer_12_out, multiplexer_13_out, multiplexer_14_out, multiplexer_15_out,
       multiplexer_16_out, multiplexer_17_out, multiplexer_18_out, multiplexer_19_out, multiplexer_20_out,
       multiplexer_21_out, multiplexer_22_out, multiplexer_23_out, multiplexer_24_out, multiplexer_25_out,
       multiplexer_26_out, multiplexer_27_out, multiplexer_28_out, multiplexer_29_out, multiplexer_30_out,
       multiplexer_31_out, multiplexer_32_out;

  Multiplexer #(.enable("false")) multiplexer_1 (
    .in0(bitsIn[0]), .in1(bitsIn[4]), .out(multiplexer_1_out), .sel(Shamt[2]));
  Multiplexer #(.enable("false")) multiplexer_2 (
    .in0(bitsIn[1]), .in1(bitsIn[5]), .out(multiplexer_2_out), .sel(Shamt[2]));
  Multiplexer #(.enable("false")) multiplexer_3 (
    .in0(bitsIn[2]), .in1(bitsIn[6]), .out(multiplexer_3_out), .sel(Shamt[2]));
  Multiplexer #(.enable("false")) multiplexer_4 (
    .in0(bitsIn[3]), .in1(bitsIn[7]), .out(multiplexer_4_out), .sel(Shamt[2]));
  Multiplexer #(.enable("false")) multiplexer_5 (
    .in0(bitsIn[4]), .in1(bitsIn[8]), .out(multiplexer_5_out), .sel(Shamt[2]));
  Multiplexer #(.enable("false")) multiplexer_6 (
    .in0(bitsIn[5]), .in1(bitsIn[9]), .out(multiplexer_6_out), .sel(Shamt[2]));
  Multiplexer #(.enable("false")) multiplexer_7 (
    .in0(bitsIn[6]), .in1(bitsIn[10]), .out(multiplexer_7_out), .sel(Shamt[2]));
  Multiplexer #(.enable("false")) multiplexer_8 (
    .in0(bitsIn[7]), .in1(bitsIn[11]), .out(multiplexer_8_out), .sel(Shamt[2]));
  Multiplexer #(.enable("false")) multiplexer_9 (
    .in0(bitsIn[8]), .in1(bitsIn[12]), .out(multiplexer_9_out), .sel(Shamt[2]));
  Multiplexer #(.enable("false")) multiplexer_10 (
    .in0(bitsIn[9]), .in1(bitsIn[13]), .out(multiplexer_10_out), .sel(Shamt[2]));
  Multiplexer #(.enable("false")) multiplexer_11 (
    .in0(bitsIn[10]), .in1(bitsIn[14]), .out(multiplexer_11_out), .sel(Shamt[2]));
  Multiplexer #(.enable("false")) multiplexer_12 (
    .in0(bitsIn[11]), .in1(bitsIn[15]), .out(multiplexer_12_out), .sel(Shamt[2]));
  Multiplexer #(.enable("false")) multiplexer_13 (
    .in0(bitsIn[12]), .in1(1'b0), .out(multiplexer_13_out), .sel(Shamt[2]));
  Multiplexer #(.enable("false")) multiplexer_14 (
    .in0(bitsIn[13]), .in1(1'b0), .out(multiplexer_14_out), .sel(Shamt[2]));
  Multiplexer #(.enable("false")) multiplexer_15 (
    .in0(bitsIn[14]), .in1(1'b0), .out(multiplexer_15_out), .sel(Shamt[2]));
  Multiplexer #(.enable("false")) multiplexer_16 (
    .in0(bitsIn[15]), .in1(1'b0), .out(multiplexer_16_out), .sel(Shamt[2]));
  Multiplexer #(.enable("false")) multiplexer_17 (
    .in0(multiplexer_1_out), .in1(multiplexer_3_out), .out(multiplexer_17_out), .sel(Shamt[1]));
  Multiplexer #(.enable("false")) multiplexer_18 (
    .in0(multiplexer_2_out), .in1(multiplexer_4_out), .out(multiplexer_18_out), .sel(Shamt[1]));
  Multiplexer #(.enable("false")) multiplexer_19 (
    .in0(multiplexer_3_out), .in1(multiplexer_5_out), .out(multiplexer_19_out), .sel(Shamt[1]));
  Multiplexer #(.enable("false")) multiplexer_20 (
    .in0(multiplexer_4_out), .in1(multiplexer_6_out), .out(multiplexer_20_out), .sel(Shamt[1]));
  Multiplexer #(.enable("false")) multiplexer_21 (
    .in0(multiplexer_5_out), .in1(multiplexer_7_out), .out(multiplexer_21_out), .sel(Shamt[1]));
  Multiplexer #(.enable("false")) multiplexer_22 (
    .in0(multiplexer_6_out), .in1(multiplexer_8_out), .out(multiplexer_22_out), .sel(Shamt[1]));
  Multiplexer #(.enable("false")) multiplexer_23 (
    .in0(multiplexer_7_out), .in1(multiplexer_9_out), .out(multiplexer_23_out), .sel(Shamt[1]));
  Multiplexer #(.enable("false")) multiplexer_24 (
    .in0(multiplexer_8_out), .in1(multiplexer_10_out), .out(multiplexer_24_out), .sel(Shamt[1]));
  Multiplexer #(.enable("false")) multiplexer_25 (
    .in0(multiplexer_9_out), .in1(multiplexer_11_out), .out(multiplexer_25_out), .sel(Shamt[1]));
  Multiplexer #(.enable("false")) multiplexer_26 (
    .in0(multiplexer_10_out), .in1(multiplexer_12_out), .out(multiplexer_26_out), .sel(Shamt[1]));
  Multiplexer #(.enable("false")) multiplexer_27 (
    .in0(multiplexer_11_out), .in1(multiplexer_13_out), .out(multiplexer_27_out), .sel(Shamt[1]));
  Multiplexer #(.enable("false")) multiplexer_28 (
    .in0(multiplexer_12_out), .in1(multiplexer_14_out), .out(multiplexer_28_out), .sel(Shamt[1]));
  Multiplexer #(.enable("false")) multiplexer_29 (
    .in0(multiplexer_13_out), .in1(multiplexer_15_out), .out(multiplexer_29_out), .sel(Shamt[1]));
  Multiplexer #(.enable("false")) multiplexer_30 (
    .in0(multiplexer_14_out), .in1(multiplexer_16_out), .out(multiplexer_30_out), .sel(Shamt[1]));
  Multiplexer #(.enable("false")) multiplexer_31 (
    .in0(multiplexer_15_out), .in1(1'b0), .out(multiplexer_31_out), .sel(Shamt[1]));
  Multiplexer #(.enable("false")) multiplexer_32 (
    .in0(multiplexer_16_out), .in1(1'b0), .out(multiplexer_32_out), .sel(Shamt[1]));
  Multiplexer #(.enable("false")) multiplexer_33 (
    .in0(multiplexer_17_out), .in1(multiplexer_18_out), .out(shifted_out[0]), .sel(Shamt[0]));
  Multiplexer #(.enable("false")) multiplexer_34 (
    .in0(multiplexer_18_out), .in1(multiplexer_19_out), .out(shifted_out[1]), .sel(Shamt[0]));
  Multiplexer #(.enable("false")) multiplexer_35 (
    .in0(multiplexer_19_out), .in1(multiplexer_20_out), .out(shifted_out[2]), .sel(Shamt[0]));
  Multiplexer #(.enable("false")) multiplexer_36 (
    .in0(multiplexer_20_out), .in1(multiplexer_21_out), .out(shifted_out[3]), .sel(Shamt[0]));
  Multiplexer #(.enable("false")) multiplexer_37 (
    .in0(multiplexer_21_out), .in1(multiplexer_22_out), .out(shifted_out[4]), .sel(Shamt[0]));
  Multiplexer #(.enable("false")) multiplexer_38 (
    .in0(multiplexer_22_out), .in1(multiplexer_23_out), .out(shifted_out[5]), .sel(Shamt[0]));
  Multiplexer #(.enable("false")) multiplexer_39 (
    .in0(multiplexer_23_out), .in1(multiplexer_24_out), .out(shifted_out[6]), .sel(Shamt[0]));
  Multiplexer #(.enable("false")) multiplexer_40 (
    .in0(multiplexer_24_out), .in1(multiplexer_25_out), .out(shifted_out[7]), .sel(Shamt[0]));
  Multiplexer #(.enable("false")) multiplexer_41 (
    .in0(multiplexer_25_out), .in1(multiplexer_26_out), .out(shifted_out[8]), .sel(Shamt[0]));
  Multiplexer #(.enable("false")) multiplexer_42 (
    .in0(multiplexer_26_out), .in1(multiplexer_27_out), .out(shifted_out[9]), .sel(Shamt[0]));
  Multiplexer #(.enable("false")) multiplexer_43 (
    .in0(multiplexer_27_out), .in1(multiplexer_28_out), .out(shifted_out[10]), .sel(Shamt[0]));
  Multiplexer #(.enable("false")) multiplexer_44 (
    .in0(multiplexer_28_out), .in1(multiplexer_29_out), .out(shifted_out[11]), .sel(Shamt[0]));
  Multiplexer #(.enable("false")) multiplexer_45 (
    .in0(multiplexer_29_out), .in1(multiplexer_30_out), .out(shifted_out[12]), .sel(Shamt[0]));
  Multiplexer #(.enable("false")) multiplexer_46 (
    .in0(multiplexer_30_out), .in1(multiplexer_31_out), .out(shifted_out[13]), .sel(Shamt[0]));
  Multiplexer #(.enable("false")) multiplexer_47 (
    .in0(multiplexer_31_out), .in1(multiplexer_32_out), .out(shifted_out[14]), .sel(Shamt[0]));
  Multiplexer #(.enable("false")) multiplexer_48 (
    .in0(multiplexer_32_out), .in1(1'b0), .out(shifted_out[15]), .sel(Shamt[0]));

  // Other names for the same wires on the sheet: a0 = bitsIn[0]; a1 = bitsIn[1]; a2 = bitsIn[2]; a3 = bitsIn[3];
  //   a4 = bitsIn[4]; a5 = bitsIn[5]; a6 = bitsIn[6]; a7 = bitsIn[7]; a8 = bitsIn[8]; a9 = bitsIn[9];
  //   a10 = bitsIn[10]; a11 = bitsIn[11]; a12 = bitsIn[12]; a13 = bitsIn[13]; a14 = bitsIn[14]; a15 = bitsIn[15];
  //   s0 = Shamt[0]; s1 = Shamt[1]; s2 = Shamt[2]; o0 = shifted_out[0]; o1 = shifted_out[1]; o2 = shifted_out[2];
  //   o3 = shifted_out[3]; o4 = shifted_out[4]; o5 = shifted_out[5]; o6 = shifted_out[6]; o7 = shifted_out[7];
  //   o8 = shifted_out[8]; o9 = shifted_out[9]; o10 = shifted_out[10]; o11 = shifted_out[11]; o12 = shifted_out[12];
  //   o13 = shifted_out[13]; o14 = shifted_out[14]; o15 = shifted_out[15]

  // Notes on the sheet:
  //   shift by 4
  //   shift by 2
  //   shift by 1
endmodule

module left_shift (
  input  [15:0] bitsIn,
  input  [2:0] Shamt,
  output [15:0] shifted_out
);

  wire multiplexer_1_out, multiplexer_2_out, multiplexer_3_out, multiplexer_4_out, multiplexer_5_out,
       multiplexer_6_out, multiplexer_7_out, multiplexer_8_out, multiplexer_9_out, multiplexer_10_out,
       multiplexer_11_out, multiplexer_12_out, multiplexer_13_out, multiplexer_14_out, multiplexer_15_out,
       multiplexer_16_out, multiplexer_17_out, multiplexer_18_out, multiplexer_19_out, multiplexer_20_out,
       multiplexer_21_out, multiplexer_22_out, multiplexer_23_out, multiplexer_24_out, multiplexer_25_out,
       multiplexer_26_out, multiplexer_27_out, multiplexer_28_out, multiplexer_29_out, multiplexer_30_out,
       multiplexer_31_out, multiplexer_32_out;

  Multiplexer #(.enable("false")) multiplexer_1 (
    .in0(bitsIn[15]), .in1(bitsIn[11]), .out(multiplexer_1_out), .sel(Shamt[2]));
  Multiplexer #(.enable("false")) multiplexer_2 (
    .in0(bitsIn[14]), .in1(bitsIn[10]), .out(multiplexer_2_out), .sel(Shamt[2]));
  Multiplexer #(.enable("false")) multiplexer_3 (
    .in0(bitsIn[13]), .in1(bitsIn[9]), .out(multiplexer_3_out), .sel(Shamt[2]));
  Multiplexer #(.enable("false")) multiplexer_4 (
    .in0(bitsIn[12]), .in1(bitsIn[8]), .out(multiplexer_4_out), .sel(Shamt[2]));
  Multiplexer #(.enable("false")) multiplexer_5 (
    .in0(bitsIn[11]), .in1(bitsIn[7]), .out(multiplexer_5_out), .sel(Shamt[2]));
  Multiplexer #(.enable("false")) multiplexer_6 (
    .in0(bitsIn[10]), .in1(bitsIn[6]), .out(multiplexer_6_out), .sel(Shamt[2]));
  Multiplexer #(.enable("false")) multiplexer_7 (
    .in0(bitsIn[9]), .in1(bitsIn[5]), .out(multiplexer_7_out), .sel(Shamt[2]));
  Multiplexer #(.enable("false")) multiplexer_8 (
    .in0(bitsIn[8]), .in1(bitsIn[4]), .out(multiplexer_8_out), .sel(Shamt[2]));
  Multiplexer #(.enable("false")) multiplexer_9 (
    .in0(bitsIn[7]), .in1(bitsIn[3]), .out(multiplexer_9_out), .sel(Shamt[2]));
  Multiplexer #(.enable("false")) multiplexer_10 (
    .in0(bitsIn[6]), .in1(bitsIn[2]), .out(multiplexer_10_out), .sel(Shamt[2]));
  Multiplexer #(.enable("false")) multiplexer_11 (
    .in0(bitsIn[5]), .in1(bitsIn[1]), .out(multiplexer_11_out), .sel(Shamt[2]));
  Multiplexer #(.enable("false")) multiplexer_12 (
    .in0(bitsIn[4]), .in1(bitsIn[0]), .out(multiplexer_12_out), .sel(Shamt[2]));
  Multiplexer #(.enable("false")) multiplexer_13 (
    .in0(bitsIn[3]), .in1(1'b0), .out(multiplexer_13_out), .sel(Shamt[2]));
  Multiplexer #(.enable("false")) multiplexer_14 (
    .in0(bitsIn[2]), .in1(1'b0), .out(multiplexer_14_out), .sel(Shamt[2]));
  Multiplexer #(.enable("false")) multiplexer_15 (
    .in0(bitsIn[1]), .in1(1'b0), .out(multiplexer_15_out), .sel(Shamt[2]));
  Multiplexer #(.enable("false")) multiplexer_16 (
    .in0(bitsIn[0]), .in1(1'b0), .out(multiplexer_16_out), .sel(Shamt[2]));
  Multiplexer #(.enable("false")) multiplexer_17 (
    .in0(multiplexer_1_out), .in1(multiplexer_3_out), .out(multiplexer_17_out), .sel(Shamt[1]));
  Multiplexer #(.enable("false")) multiplexer_18 (
    .in0(multiplexer_2_out), .in1(multiplexer_4_out), .out(multiplexer_18_out), .sel(Shamt[1]));
  Multiplexer #(.enable("false")) multiplexer_19 (
    .in0(multiplexer_3_out), .in1(multiplexer_5_out), .out(multiplexer_19_out), .sel(Shamt[1]));
  Multiplexer #(.enable("false")) multiplexer_20 (
    .in0(multiplexer_4_out), .in1(multiplexer_6_out), .out(multiplexer_20_out), .sel(Shamt[1]));
  Multiplexer #(.enable("false")) multiplexer_21 (
    .in0(multiplexer_5_out), .in1(multiplexer_7_out), .out(multiplexer_21_out), .sel(Shamt[1]));
  Multiplexer #(.enable("false")) multiplexer_22 (
    .in0(multiplexer_6_out), .in1(multiplexer_8_out), .out(multiplexer_22_out), .sel(Shamt[1]));
  Multiplexer #(.enable("false")) multiplexer_23 (
    .in0(multiplexer_7_out), .in1(multiplexer_9_out), .out(multiplexer_23_out), .sel(Shamt[1]));
  Multiplexer #(.enable("false")) multiplexer_24 (
    .in0(multiplexer_8_out), .in1(multiplexer_10_out), .out(multiplexer_24_out), .sel(Shamt[1]));
  Multiplexer #(.enable("false")) multiplexer_25 (
    .in0(multiplexer_9_out), .in1(multiplexer_11_out), .out(multiplexer_25_out), .sel(Shamt[1]));
  Multiplexer #(.enable("false")) multiplexer_26 (
    .in0(multiplexer_10_out), .in1(multiplexer_12_out), .out(multiplexer_26_out), .sel(Shamt[1]));
  Multiplexer #(.enable("false")) multiplexer_27 (
    .in0(multiplexer_11_out), .in1(multiplexer_13_out), .out(multiplexer_27_out), .sel(Shamt[1]));
  Multiplexer #(.enable("false")) multiplexer_28 (
    .in0(multiplexer_12_out), .in1(multiplexer_14_out), .out(multiplexer_28_out), .sel(Shamt[1]));
  Multiplexer #(.enable("false")) multiplexer_29 (
    .in0(multiplexer_13_out), .in1(multiplexer_15_out), .out(multiplexer_29_out), .sel(Shamt[1]));
  Multiplexer #(.enable("false")) multiplexer_30 (
    .in0(multiplexer_14_out), .in1(multiplexer_16_out), .out(multiplexer_30_out), .sel(Shamt[1]));
  Multiplexer #(.enable("false")) multiplexer_31 (
    .in0(multiplexer_15_out), .in1(1'b0), .out(multiplexer_31_out), .sel(Shamt[1]));
  Multiplexer #(.enable("false")) multiplexer_32 (
    .in0(multiplexer_16_out), .in1(1'b0), .out(multiplexer_32_out), .sel(Shamt[1]));
  Multiplexer #(.enable("false")) multiplexer_33 (
    .in0(multiplexer_17_out), .in1(multiplexer_18_out), .out(shifted_out[15]), .sel(Shamt[0]));
  Multiplexer #(.enable("false")) multiplexer_34 (
    .in0(multiplexer_18_out), .in1(multiplexer_19_out), .out(shifted_out[14]), .sel(Shamt[0]));
  Multiplexer #(.enable("false")) multiplexer_35 (
    .in0(multiplexer_19_out), .in1(multiplexer_20_out), .out(shifted_out[13]), .sel(Shamt[0]));
  Multiplexer #(.enable("false")) multiplexer_36 (
    .in0(multiplexer_20_out), .in1(multiplexer_21_out), .out(shifted_out[12]), .sel(Shamt[0]));
  Multiplexer #(.enable("false")) multiplexer_37 (
    .in0(multiplexer_21_out), .in1(multiplexer_22_out), .out(shifted_out[11]), .sel(Shamt[0]));
  Multiplexer #(.enable("false")) multiplexer_38 (
    .in0(multiplexer_22_out), .in1(multiplexer_23_out), .out(shifted_out[10]), .sel(Shamt[0]));
  Multiplexer #(.enable("false")) multiplexer_39 (
    .in0(multiplexer_23_out), .in1(multiplexer_24_out), .out(shifted_out[9]), .sel(Shamt[0]));
  Multiplexer #(.enable("false")) multiplexer_40 (
    .in0(multiplexer_24_out), .in1(multiplexer_25_out), .out(shifted_out[8]), .sel(Shamt[0]));
  Multiplexer #(.enable("false")) multiplexer_41 (
    .in0(multiplexer_25_out), .in1(multiplexer_26_out), .out(shifted_out[7]), .sel(Shamt[0]));
  Multiplexer #(.enable("false")) multiplexer_42 (
    .in0(multiplexer_26_out), .in1(multiplexer_27_out), .out(shifted_out[6]), .sel(Shamt[0]));
  Multiplexer #(.enable("false")) multiplexer_43 (
    .in0(multiplexer_27_out), .in1(multiplexer_28_out), .out(shifted_out[5]), .sel(Shamt[0]));
  Multiplexer #(.enable("false")) multiplexer_44 (
    .in0(multiplexer_28_out), .in1(multiplexer_29_out), .out(shifted_out[4]), .sel(Shamt[0]));
  Multiplexer #(.enable("false")) multiplexer_45 (
    .in0(multiplexer_29_out), .in1(multiplexer_30_out), .out(shifted_out[3]), .sel(Shamt[0]));
  Multiplexer #(.enable("false")) multiplexer_46 (
    .in0(multiplexer_30_out), .in1(multiplexer_31_out), .out(shifted_out[2]), .sel(Shamt[0]));
  Multiplexer #(.enable("false")) multiplexer_47 (
    .in0(multiplexer_31_out), .in1(multiplexer_32_out), .out(shifted_out[1]), .sel(Shamt[0]));
  Multiplexer #(.enable("false")) multiplexer_48 (
    .in0(multiplexer_32_out), .in1(1'b0), .out(shifted_out[0]), .sel(Shamt[0]));

  // Other names for the same wires on the sheet: a0 = bitsIn[0]; a1 = bitsIn[1]; a2 = bitsIn[2]; a3 = bitsIn[3];
  //   a4 = bitsIn[4]; a5 = bitsIn[5]; a6 = bitsIn[6]; a7 = bitsIn[7]; a8 = bitsIn[8]; a9 = bitsIn[9];
  //   a10 = bitsIn[10]; a11 = bitsIn[11]; a12 = bitsIn[12]; a13 = bitsIn[13]; a14 = bitsIn[14]; a15 = bitsIn[15];
  //   s0 = Shamt[0]; s1 = Shamt[1]; s2 = Shamt[2]; o0 = shifted_out[0]; o1 = shifted_out[1]; o2 = shifted_out[2];
  //   o3 = shifted_out[3]; o4 = shifted_out[4]; o5 = shifted_out[5]; o6 = shifted_out[6]; o7 = shifted_out[7];
  //   o8 = shifted_out[8]; o9 = shifted_out[9]; o10 = shifted_out[10]; o11 = shifted_out[11]; o12 = shifted_out[12];
  //   o13 = shifted_out[13]; o14 = shifted_out[14]; o15 = shifted_out[15]

  // Notes on the sheet:
  //   shift by 4
  //   shift by 2
  //   shift by 1
endmodule

module memory_latch (
  input  [15:0] address,
  input  WE,
  input  clk,
  input  [15:0] data_in,
  output [15:0] address_latched,
  output WE_latched,
  output OE_latched,
  output [15:0] data_in_latched
);

  wire DMwe_latch_q;
  wire [15:0] addr_latch_q;

  Register #(.width(16), .trigger("falling")) addr_latch (
    .D(address), .en(WE), .clk(clk), .Q(addr_latch_q));  // open: clr
  D_Flip_Flop #(.trigger("falling")) DMwe_latch (.D(WE), .clk(clk), .Q(DMwe_latch_q));  // open: Qn, preset, reset
  Register #(.width(16), .trigger("falling")) data_to_be_written (
    .D(data_in), .en(WE), .clk(clk), .Q(data_in_latched));  // open: clr
  Multiplexer #(.width(16), .enable("false")) multiplexer_1 (
    .in0(address), .in1(addr_latch_q), .out(address_latched), .sel(DMwe_latch_q));
  and and_1 (WE_latched, clk, DMwe_latch_q);
  not not_1 (OE_latched, WE_latched);
endmodule

module InstructionDecode (
  input  [15:0] input_16_bits,
  output [2:0] Shamt,
  output [2:0] Rd,
  output [2:0] Rt,
  output [2:0] Rs,
  output lw,
  output sw,
  output iType,
  output bgez,
  output beq,
  output readKeyboard,
  output TTY,
  output j,
  output jr,
  output jal
);

  wire and_2_out, and_3_out, and_4_out, and_5_out, not_1_out, not_2_out, not_3_out, not_4_out, not_5_out,
       not_6_out, not_7_out, not_8_out, not_9_out, not_10_out, not_11_out, not_12_out, not_13_out,
       not_14_out, not_15_out, not_16_out, not_17_out, not_18_out, not_19_out, not_20_out, not_21_out;

  not not_1 (not_1_out, input_16_bits[13]);
  not not_2 (not_2_out, input_16_bits[14]);
  not not_3 (not_3_out, input_16_bits[14]);
  not not_4 (not_4_out, input_16_bits[14]);
  not not_5 (not_5_out, input_16_bits[15]);
  not not_6 (not_6_out, input_16_bits[14]);
  not not_7 (not_7_out, input_16_bits[12]);
  not not_8 (not_8_out, input_16_bits[12]);
  not not_9 (not_9_out, input_16_bits[13]);
  not not_10 (not_10_out, input_16_bits[15]);
  not not_11 (not_11_out, input_16_bits[13]);
  not not_12 (not_12_out, input_16_bits[13]);
  and and_1 (j, input_16_bits[15], not_4_out, input_16_bits[13], input_16_bits[12]);
  and and_2 (and_2_out, not_5_out, input_16_bits[14], input_16_bits[13], input_16_bits[12]);
  and and_3 (and_3_out, not_6_out, not_1_out, not_7_out);
  and and_4 (and_4_out, input_16_bits[15], not_2_out, not_8_out);
  and and_5 (and_5_out, input_16_bits[15], not_3_out, not_9_out);
  and and_6 (lw, not_10_out, input_16_bits[14], input_16_bits[13], input_16_bits[12]);
  not not_13 (not_13_out, input_16_bits[14]);
  not not_14 (not_14_out, input_16_bits[12]);
  not not_15 (not_15_out, input_16_bits[14]);
  not not_16 (not_16_out, input_16_bits[14]);
  not not_17 (not_17_out, input_16_bits[12]);
  and and_7 (sw, input_16_bits[15], not_13_out, not_11_out, not_14_out);
  and and_8 (bgez, input_16_bits[15], not_15_out, not_12_out, input_16_bits[12]);
  and and_9 (beq, input_16_bits[15], not_16_out, input_16_bits[13], not_17_out);
  or or_1 (iType, and_2_out, and_3_out, and_4_out, and_5_out);
  not not_18 (not_18_out, input_16_bits[13]);
  not not_19 (not_19_out, input_16_bits[12]);
  and and_10 (jr, input_16_bits[15], input_16_bits[14], not_18_out, not_19_out);
  not not_20 (not_20_out, input_16_bits[12]);
  and and_11 (readKeyboard, input_16_bits[15], input_16_bits[14], input_16_bits[13], not_20_out);
  and and_12 (TTY, input_16_bits[15], input_16_bits[14], input_16_bits[13], input_16_bits[12]);
  not not_21 (not_21_out, input_16_bits[13]);
  and and_13 (jal, input_16_bits[15], input_16_bits[14], not_21_out, input_16_bits[12]);

  assign Rd = input_16_bits[5:3];
  assign Rs = input_16_bits[11:9];
  assign Rt = input_16_bits[8:6];
  assign Shamt = input_16_bits[2:0];

  // Other names for the same wires on the sheet: keyboard_input = readKeyboard; op0 = input_16_bits[12];
  //   Opcode[3:0] = input_16_bits[15:12]; op1 = input_16_bits[13]; op2 = input_16_bits[14]; op3 = input_16_bits[15];
  //   TTY_output = TTY

  // Notes on the sheet:
  //   Outputs!
  //   Decode OpCode
endmodule
